// Logisim project Machine.circ as structural Verilog: 2 circuits, main circuit main
module main (
);

  wire Clk_Button_out, Rst_Button_out;
  wire [7:0] RAM_Addr, ROM_Addr;
  wire [15:0] ROM_1_data_2;
  wire [31:0] CPU_1_r0, CPU_1_r1, CPU_1_r2, CPU_1_r3, CPU_1_r4, CPU_1_r5, CPU_1_r6, CPU_1_r7, rom_1_data;

  // Probe on RAM_Addr
  ROM #(.dataWidth(32)) rom_1 (.addr(RAM_Addr), .data(rom_1_data));
  Button Clk_Button (.out(Clk_Button_out));
  Button Rst_Button (.out(Rst_Button_out));
  // Probe on ROM_Addr
  ROM #(.dataWidth(16)) ROM_1_dup2 (.addr(ROM_Addr), .data(ROM_1_data_2));
  // Probe on CPU_1_r3
  // Probe on CPU_1_r2
  // Probe on CPU_1_r1
  // Probe on CPU_1_r0
  // Probe on CPU_1_r7
  // Probe on CPU_1_r6
  // Probe on CPU_1_r5
  // Probe on CPU_1_r4
  CPU CPU_1 (
    .RAM_In(rom_1_data), .RAM_Addr(RAM_Addr), .Clk(Clk_Button_out), .ROM_In(ROM_1_data_2),
    .Rst(Rst_Button_out), .ROM_Addr(ROM_Addr), .R0(CPU_1_r0), .R1(CPU_1_r1), .R2(CPU_1_r2), .R3(CPU_1_r3),
    .R4(CPU_1_r4), .R5(CPU_1_r5), .R6(CPU_1_r6), .R7(CPU_1_r7));  // open: RAM_Out

  // Notes on the sheet:
  //   contents of rom_1 (hex, n*v repeats v):
  //   1 3 2 4
  //   contents of ROM_1 (hex, n*v repeats v):
  //   9800 9900 1a08 d005 9a02 9801 c9 4308
endmodule

module CPU (
  input  [31:0] RAM_In,
  input  [15:0] ROM_In,
  input  Clk,
  input  Rst,
  output [7:0] ROM_Addr,
  output [7:0] RAM_Addr,
  output [31:0] RAM_Out,
  output [31:0] R3,
  output [31:0] R7,
  output [31:0] R2,
  output [31:0] R6,
  output [31:0] R1,
  output [31:0] R5,
  output [31:0] R0,
  output [31:0] R4
);

  wire Ctrl_1_load, Ctrl_1_shifterimme;
  wire [2:0] Ctrl_1_rd, Ctrl_1_rm, Ctrl_1_rn;
  wire [3:0] ALU_1_flags, Ctrl_1_codop;
  wire [4:0] Ctrl_1_imm5, multiplexer_2_out;
  wire [31:0] ALU_1_s, multiplexer_1_out, Regs_1_p15;

  mainControl Ctrl_1 (
    .Inst(ROM_In), .Clk(Clk), .Reset(Rst), .PCOut(ROM_Addr), .Codop(Ctrl_1_codop), .Rm(Ctrl_1_rm),
    .Rd(Ctrl_1_rd), .Rn(Ctrl_1_rn), .Imm8(RAM_Addr), .Imm5(Ctrl_1_imm5), .Flags(ALU_1_flags),
    .Load(Ctrl_1_load), .ShifterImme(Ctrl_1_shifterimme));  // open: Store
  Multiplexer #(.width(32), .enable("false")) multiplexer_1 (
    .in0(ALU_1_s), .in1(RAM_In), .out(multiplexer_1_out), .sel(Ctrl_1_load));
  // BancRegistre Regs_1: pin names not known; wires that end beside it: multiplexer_1_out, Ctrl_1_rd, Clk, R0, Rst, R1, R2, R3, R4, Ctrl_1_rm, R5, R6, Ctrl_1_rn, R7, Regs_1_p15, RAM_Out
  ALU ALU_1 (
    .Codop(Ctrl_1_codop), .CarryIn(ALU_1_flags[2]), .A(RAM_Out), .B(Regs_1_p15), .Shift(multiplexer_2_out),
    .S(ALU_1_s), .Flags(ALU_1_flags));
  Multiplexer #(.width(5), .enable("false")) multiplexer_2 (
    .in0(RAM_Out[4:0]), .in1(Ctrl_1_imm5), .out(multiplexer_2_out), .sel(Ctrl_1_shifterimme));

  // Notes on the sheet:
  //   Use data from register or immediate for shift
  //   RAM/ALU Input selector
endmodule
